// Digital circuit 8bit_adder.dig as structural Verilog
module _8bit_adder (
  input  [7:0] A,
  input  [7:0] B,
  input  Ci,
  output [7:0] S,
  output Ci_out
);

  // full_adder full_adder_1: pin names not known; wires that end beside it: A[0], B[0], Ci, S[0], Ci_out
  // full_adder full_adder_2: pin names not known; wires that end beside it: A[1], B[1], Ci, S[1], Ci_out
  // full_adder full_adder_3: pin names not known; wires that end beside it: A[2], B[2], Ci, S[2], Ci_out
  // full_adder full_adder_4: pin names not known; wires that end beside it: A[3], B[3], Ci, S[3], Ci_out
  // full_adder full_adder_5: pin names not known; wires that end beside it: A[4], A[7], Ci, S[4], Ci_out
  // full_adder full_adder_6: pin names not known; wires that end beside it: A[7], B[5], Ci, S[5], Ci_out
  // full_adder full_adder_7: pin names not known; wires that end beside it: A[7], B[6], Ci, S[6], Ci_out
  // full_adder full_adder_8: pin names not known; wires that end beside it: A[7], B[7], Ci, S[7], Ci_out
  // Pins of 1 and 8 bits meet at S

  assign A[6:5] = {2{A[7]}};
  assign B[4] = A[7];
endmodule
