// Digital circuit 8bit_decrementor.dig as structural Verilog
module _8bit_decrementor (
  input  [7:0] A_in,
  output [7:0] S_out
);

  _8bit_adder _8bit_adder_1 (.A(A_in), .B({8{1'b1}}), .Ci(1'b0), .S(S_out));  // open: Ci_out
endmodule
