// Digital circuit 8bit_subtractor.dig as structural Verilog
module _8bit_subtractor (
  input  [7:0] A,
  input  [7:0] B,
  output [7:0] S
);

  _8bit_adder _8bit_adder_1 (.A(A), .B(B), .Ci(1'b1), .S(S));  // open: Ci_out
endmodule
