// Digital circuit 8bit_adder.dig as structural Verilog
module _8bit_adder (
  input  [7:0] A,
  input  [7:0] B,
  input  Ci,
  output [7:0] S,
  output Ci_out
);

  wire full_adder_1_p5, full_adder_2_p5, full_adder_3_p5, full_adder_4_p5, full_adder_5_p5, full_adder_6_p5,
       full_adder_7_p5;

  // full_adder full_adder_1: pin names not known; wires that end beside it: A[0], B[0], Ci, S[0], full_adder_1_p5
  // full_adder full_adder_2: pin names not known; wires that end beside it: A[1], B[1], full_adder_1_p5, S[1], full_adder_2_p5
  // full_adder full_adder_3: pin names not known; wires that end beside it: A[2], B[2], full_adder_2_p5, S[2], full_adder_3_p5
  // full_adder full_adder_4: pin names not known; wires that end beside it: A[3], B[3], full_adder_3_p5, S[3], full_adder_4_p5
  // full_adder full_adder_5: pin names not known; wires that end beside it: A[4], B[4], full_adder_4_p5, S[4], full_adder_5_p5
  // full_adder full_adder_6: pin names not known; wires that end beside it: A[5], B[5], full_adder_5_p5, S[5], full_adder_6_p5
  // full_adder full_adder_7: pin names not known; wires that end beside it: A[6], B[6], full_adder_6_p5, S[6], full_adder_7_p5
  // full_adder full_adder_8: pin names not known; wires that end beside it: A[7], B[7], full_adder_7_p5, S[7], Ci_out

  // Other names for the same wires on the sheet: CIN = Ci
endmodule
