// Digital circuit CPU.dig as structural Verilog
module CPU (
  input  CLK,
  input  RST
);

  wire CPU_CLK, HLT, IR_ld, MAR_ld, not_1_out, OpCode, OUT_ld, PC_en, PC_ld, PC_out, RegA_ld, RegB_ld,
       ULA_op, WBus_sel, Z_Flag;
  wire [3:0] OUT_Reg_q_out, OUT_Reg_q_out_2;
  wire [7:0] MEM_data, W_bus;

  ResettableRegister OUT_Reg (
    .D_in(W_bus), .CLK(CPU_CLK), .Ld(OUT_ld), .RST(RST), .Q_out({OUT_Reg_q_out_2, OUT_Reg_q_out}));
  not not_1 (not_1_out, HLT);
  Seven_Seg_Hex seven_seg_hex_1 (.d(OUT_Reg_q_out_2), .dp(1'b0));
  and and_1 (CPU_CLK, not_1_out, CLK);
  Seven_Seg_Hex seven_seg_hex_2 (.d(OUT_Reg_q_out), .dp(1'b0));
  memory memory_1 (.WBus_in(W_bus), .MAR_LD(MAR_ld), .CLK(CPU_CLK), .RST(RST), .Data_Out(MEM_data));
  // newPC newpc_1: pin names not known; wires that end beside it: W_bus, PC_en, PC_ld, CPU_CLK, RST, PC_out
  // ControlUnit controlunit_1: pin names not known; wires that end beside it: OpCode, Z_Flag, CPU_CLK, RST, WBus_sel, PC_en, PC_ld, MAR_ld, IR_ld, RegA_ld, RegB_ld, OUT_ld, ULA_op, HLT
  // DataPath datapath_1: pin names not known; wires that end beside it: W_bus, RegA_ld, RegB_ld, IR_ld, ULA_op, WBus_sel, CPU_CLK, RST, MEM_data, PC_out, W_bus, OpCode, Z_Flag

  // Notes on the sheet:
  //   CLK: Hz: 3
endmodule
