// Digital circuit ControlUnit.dig as structural Verilog
module ControlUnit (
  input  [3:0] OpCode_in,
  input  ZFlag_in,
  input  CLK,
  input  RST,
  output [2:0] WBus_Sel,
  output PC_en,
  output PC_ld,
  output MAR_ld,
  output IR_ld,
  output RegA_ld,
  output RegB_ld,
  output OUT_ld,
  output [3:0] ULA_op,
  output HLT
);

  wire ADD_sig, and_1_out, and_2_out, and_3_out, and_4_out, and_5_out, and_8_out, and_9_out, DEC_sig,
       DIV_sig, HLT_sig, INC_sig, JMP_sig, JMPZ_sig, LDA_sig, MULT_sig, or_1_out, or_2_out, or_5_out, out_1,
       out_11, out_12, out_13, out_14, OUT_sig, SUB_sig, T1, T4, T5, T6;
  wire [2:0] priorityencoder_1_num;

  sequenciator sequenciator_1 (.CLK(CLK), .RST(RST), .T1(T1), .T2(PC_en), .T3(IR_ld), .T4(T4), .T5(T5), .T6(T6));
  and and_1 (and_1_out, LDA_sig, T5);
  or or_1 (or_1_out, SUB_sig, ADD_sig, MULT_sig, DIV_sig);
  or or_2 (or_2_out, DEC_sig, INC_sig);
  and and_2 (and_2_out, or_1_out, T6);
  and and_3 (and_3_out, T4, or_2_out);
  and and_4 (and_4_out, JMP_sig, T4);
  and and_5 (and_5_out, JMPZ_sig, ZFlag_in, T4);
  or or_3 (RegA_ld, and_1_out, and_2_out, and_3_out);
  or or_4 (PC_ld, and_4_out, and_5_out);
  and and_6 (RegB_ld, T5, or_1_out);
  and and_7 (OUT_ld, OUT_sig, T4);
  or or_5 (or_5_out, LDA_sig, ADD_sig, SUB_sig, MULT_sig, DIV_sig);
  and and_8 (and_8_out, or_5_out, T4);
  and and_9 (and_9_out, HLT_sig, T4);
  or or_6 (MAR_ld, and_8_out, T1);
  RS_FF_AS rs_ff_as_1 (.S(and_9_out), .R(RST), .Q(HLT));  // open: nQ
  PriorityEncoder #(.Selector_Bits(3)) priorityencoder_1 (
    .in0(T1), .in1(PC_en), .in2(IR_ld), .in3(T4), .in4(T5), .in5(T6), .in6(1'b0), .in7(1'b0),
    .num(priorityencoder_1_num));  // open: any
  ROM #(.AddrBits(7), .Bits(7)) rom_1 (.A({OpCode_in, priorityencoder_1_num}), .sel(1'b1), .D({ULA_op, WBus_Sel}));
  Decoder #(.Selector_Bits(4)) decoder_1 (
    .sel(OpCode_in), .out_0(out_1), .out_1(LDA_sig), .out_2(ADD_sig), .out_3(SUB_sig), .out_4(MULT_sig),
    .out_5(DIV_sig), .out_6(INC_sig), .out_7(DEC_sig), .out_8(JMP_sig), .out_9(JMPZ_sig), .out_10(out_11),
    .out_11(out_12), .out_12(out_13), .out_13(out_14), .out_14(OUT_sig), .out_15(HLT_sig));

  // Other names for the same wires on the sheet: HTL = HLT; T2 = PC_en; T3 = IR_ld

  // Notes on the sheet:
  //   UNIDADE DE CONTROLE
  //   contents of rom_1 (hex, n*v repeats v):
  //   5,0,1,5*0,5,0,1,0,1,0,0,0,5,0,1,0,1,2,0,0,5,0,1,0,1,a,0,0,5,0
  //   ,1,0,1,1a,0,0,5,0,1,0,1,2a,0,0,5,0,1,32,4*0,5,0,1,3a,4*0,5,0,1
  //   ,5*0,5,0,1,37*0,5,0,1,3,4*0,5,0,1
endmodule
