// Digital circuit ProgramCounter.dig as structural Verilog
module ProgramCounter (
  input  [7:0] WBus_in,
  input  PC_en,
  input  PC_ld,
  input  CLK,
  input  RST,
  output [7:0] PC_Out
);

  CounterPreset #(.Bits(8)) counterpreset_1 (
    .en(PC_en), .C(CLK), .dir(1'b0), .in(WBus_in), .ld(PC_ld), .clr(RST), .out(PC_Out));  // open: ovf
endmodule
