// Digital circuit ULA.dig as structural Verilog
module ULA (
  input  [7:0] A_7_0,
  input  [7:0] B_7_0,
  input  [3:0] OP_3_0,
  output [7:0] RES_7_0,
  output Z
);

  wire [3:0] divisor_1_q, divisor_1_r;
  wire [7:0] _8bit_adder_1_s, _8bit_decrementor_1_s_out, _8bit_incrementor_1_s_out, _8bit_subtractor_1_s,
       multiplier_1_p, shifter_left_8bit_1_s;

  _8bit_adder _8bit_adder_1 (.A(A_7_0), .B(B_7_0), .Ci(1'b0), .S(_8bit_adder_1_s));  // open: Ci_out
  _8bit_subtractor _8bit_subtractor_1 (.A(A_7_0), .B(B_7_0), .S(_8bit_subtractor_1_s));
  shifter_left_8bit shifter_left_8bit_1 (.A(A_7_0), .S(shifter_left_8bit_1_s));
  _8bit_incrementor _8bit_incrementor_1 (.A_in(A_7_0), .S_out(_8bit_incrementor_1_s_out));
  _8bit_decrementor _8bit_decrementor_1 (.A_in(A_7_0), .S_out(_8bit_decrementor_1_s_out));
  multiplier multiplier_1 (.A(A_7_0[3:0]), .B(B_7_0[3:0]), .P(multiplier_1_p));
  divisor divisor_1 (.A(A_7_0[3:0]), .B(B_7_0[3:0]), .Q(divisor_1_q), .R(divisor_1_r));
  Multiplexer #(.Selector_Bits(4), .Bits(8)) multiplexer_1 (
    .sel(OP_3_0), .in_0(_8bit_adder_1_s), .in_1(_8bit_subtractor_1_s), .in_2(B_7_0), .in_3(multiplier_1_p),
    .in_4(shifter_left_8bit_1_s), .in_5({divisor_1_q, divisor_1_r}), .in_6(_8bit_incrementor_1_s_out),
    .in_7(_8bit_decrementor_1_s_out), .in_8({8{1'b0}}), .in_9({8{1'b0}}), .in_10({8{1'b0}}),
    .in_11({8{1'b0}}), .in_12({8{1'b0}}), .in_13({8{1'b0}}), .in_14({8{1'b0}}), .in_15({8{1'b0}}),
    .out(RES_7_0));
  nor nor_1 (Z, RES_7_0[0], RES_7_0[1], RES_7_0[2], RES_7_0[3], RES_7_0[4], RES_7_0[5], RES_7_0[6], RES_7_0[7]);
endmodule
