// Digital circuit divisor.dig as structural Verilog
module divisor (
  input  [3:0] A,
  input  [3:0] B,
  output [3:0] Q,
  output [3:0] R
);

  divide_step divide_step_1 (.R_in(4'b0000), .A_in(A[0]), .B_in(B), .R_out(R), .Q_out(Q[3]));
  divide_step divide_step_2 (.R_in(R), .A_in(A[0]), .B_in(B), .R_out(R), .Q_out(Q[2]));
  divide_step divide_step_3 (.R_in(R), .A_in(A[0]), .B_in(B), .R_out(R), .Q_out(Q[1]));
  divide_step divide_step_4 (.R_in(R), .A_in(A[0]), .B_in(B), .R_out(R), .Q_out(Q[0]));

  // Other names for the same wires on the sheet: Q_out1 = Q[3]; Q_out2 = Q[2]; Q_out3 = Q[1]; Q_out4 = Q[0]
endmodule
