// Digital circuit memory.dig as structural Verilog
module memory (
  input  [7:0] WBus_in,
  input  MAR_LD,
  input  CLK,
  input  RST,
  output [7:0] Data_Out
);

  wire [7:0] MAR_q;

  Register #(.Bits(8)) MAR (.D(WBus_in), .C(CLK), .en(MAR_LD), .Q(MAR_q));
  ROM #(.AddrBits(8), .Bits(8)) rom_1 (.A(MAR_q), .sel(1'b1), .D(Data_Out));

  // Notes on the sheet:
  //   MEMORIA
  //   contents of rom_1 (hex, n*v repeats v):
  //   1f,3e,70,e0,97,82,0,f0,6*0,4,7,224*0,3
endmodule
