// Digital circuit sequenciator.dig as structural Verilog
module sequenciator (
  input  CLK,
  input  RST,
  output T1,
  output T2,
  output T3,
  output T4,
  output T5,
  output T6
);

  wire or_1_out, ovf;
  wire [2:0] counterpreset_1_out;

  or or_1 (or_1_out, RST, ovf);
  CounterPreset #(.maxValue(5), .Bits(3)) counterpreset_1 (
    .en(1'b1), .C(CLK), .dir(1'b0), .in(3'b000), .ld(1'b0), .clr(or_1_out), .out(counterpreset_1_out),
    .ovf(ovf));
  Decoder #(.Selector_Bits(3)) decoder_1 (
    .sel(counterpreset_1_out), .out_0(T1), .out_1(T2), .out_2(T3), .out_3(T4), .out_4(T5), .out_5(T6));  // open: out_6, out_7

  // Notes on the sheet:
  //   SEQUENCIADOR
endmodule
