// Digital circuit f_adder.dig as structural Verilog
module f_adder (
  input  A,
  input  B,
  input  Ci,
  output S,
  output Carry_Out
);

  wire half_adder_1_carry_out, half_adder_1_s, half_adder_2_carry_out;

  half_adder half_adder_1 (.A(A), .B(B), .S(half_adder_1_s), .Carry_Out(half_adder_1_carry_out));
  half_adder half_adder_2 (.A(half_adder_1_s), .B(Ci), .S(S), .Carry_Out(half_adder_2_carry_out));
  or or_1 (Carry_Out, half_adder_1_carry_out, half_adder_2_carry_out);

  // Other names for the same wires on the sheet: Ci_Out = Ci

  // Notes on the sheet:
  //   Full Adder (somador de 1 bit)
endmodule
