// Digital circuit multiplier.dig as structural Verilog
module multiplier (
  input  [3:0] A,
  input  [3:0] B,
  output [7:0] P
);

  wire C_3A, C_3B, C_4A, C_4B, C_out_1, C_out_2, C_out_3, C_out_4, C_out_5, C_outH_2, C_partial_2a, P01, P02,
       P03, P10, P11, P12, P13, P20, P21, P22, P23, P30, P31, P32, P33, S_3A, S_4A, S_partial_2;

  or or_1 (C_out_4, C_4A, C_4B);
  // full_adder fa_5a: pin names not known; wires that end beside it: P32, P23, C_out_4, P[5], C_out_5
  half_adder ha_6a (.A(P33), .B(C_out_5), .S(P[6]), .Carry_Out(P[7]));
  half_adder half_adder_1 (.A(P10), .B(P01), .S(P[1]), .Carry_Out(C_out_1));
  // full_adder fa_4a: pin names not known; wires that end beside it: P31, P22, P13, S_4A, C_4A
  half_adder ha_4a (.A(S_4A), .B(C_out_3), .S(P[4]), .Carry_Out(C_4B));
  // full_adder full_adder_1: pin names not known; wires that end beside it: P20, P11, C_out_1, S_partial_2, C_partial_2a
  or or_2 (C_out_3, C_3A, C_3B);
  // full_adder fa_3a: pin names not known; wires that end beside it: P30, P21, P12, S_3A, C_3A
  // full_adder fa_3b: pin names not known; wires that end beside it: S_3A, P03, C_out_2, P[3], C_3B
  half_adder half_adder_2 (.A(S_partial_2), .B(P02), .S(P[2]), .Carry_Out(C_outH_2));
  or or_3 (C_out_2, C_partial_2a, C_outH_2);
  and and_1 (P[0], A[0], B[0]);
  and and_2 (P10, A[1], B[0]);
  and and_3 (P20, A[2], B[0]);
  and and_4 (P30, A[3], B[0]);
  and and_5 (P02, A[0], B[2]);
  and and_6 (P12, A[1], B[2]);
  and and_7 (P22, A[2], B[2]);
  and and_8 (P32, A[3], B[2]);
  and and_9 (P01, A[0], B[1]);
  and and_10 (P11, A[1], B[1]);
  and and_11 (P21, A[2], B[1]);
  and and_12 (P31, A[3], B[1]);
  and and_13 (P03, A[0], B[3]);
  and and_14 (P13, A[1], B[3]);
  and and_15 (P23, A[2], B[3]);
  and and_16 (P33, A[3], B[3]);

  // Other names for the same wires on the sheet: C_out_6 = P[7]; P00 = P[0]

  // Notes on the sheet:
  //   MULTIPLIER
endmodule
